// Logisim project cpu16.circ as structural Verilog: 4 circuits, main circuit main
module main (
  input  zx,
  input  nx,
  input  zy,
  input  ny,
  input  f,
  input  no,
  input  [15:0] x,
  input  [15:0] y,
  output [15:0] o,
  output out_10,
  output out_11
);

  ALU alu_1 (.ny(ny), .zx(zx), .nx(nx), .f(f), .no(no), .zy(zy), .x(x), .y(y), .o(o), .zr(out_10), .ng(out_11));
endmodule

module ALU (
  input  [15:0] x,
  input  zx,
  input  nx,
  input  f,
  input  no,
  input  [15:0] y,
  input  zy,
  input  ny,
  output zr,
  output [15:0] o,
  output ng
);

  wire or_1_out;
  wire [15:0] adder_1_out, and_1_out, multiplexer_1_out, multiplexer_2_out, multiplexer_3_out,
       multiplexer_4_out, multiplexer_5_out, not_1_out, not_2_out, not_3_out;

  Multiplexer #(.width(16)) multiplexer_1 (.in0(x), .in1({16{1'b0}}), .out(multiplexer_1_out), .sel(zx));
  Multiplexer #(.width(16)) multiplexer_2 (.in0(y), .in1({16{1'b0}}), .out(multiplexer_2_out), .sel(zy));
  assign not_1_out = ~multiplexer_2_out;  // NOT_Gate not_1, 16 bits wide
  assign not_2_out = ~multiplexer_1_out;  // NOT_Gate not_2, 16 bits wide
  Multiplexer #(.width(16)) multiplexer_3 (.in0(multiplexer_2_out), .in1(not_1_out), .out(multiplexer_3_out), .sel(ny));
  Multiplexer #(.width(16)) multiplexer_4 (.in0(multiplexer_1_out), .in1(not_2_out), .out(multiplexer_4_out), .sel(nx));
  assign and_1_out = multiplexer_4_out & multiplexer_3_out;  // AND_Gate and_1, 16 bits wide
  Adder #(.width(16)) adder_1 (.a(multiplexer_4_out), .b(multiplexer_3_out), .out(adder_1_out));  // open: cin, cout
  Multiplexer #(.width(16)) multiplexer_5 (.in0(and_1_out), .in1(adder_1_out), .out(multiplexer_5_out), .sel(f));
  assign not_3_out = ~multiplexer_5_out;  // NOT_Gate not_3, 16 bits wide
  Multiplexer #(.width(16)) multiplexer_6 (.in0(multiplexer_5_out), .in1(not_3_out), .out(o), .sel(no));
  or or_1 (or_1_out, o[0], o[1], o[2], o[3], o[4], o[5], o[6], o[7], o[8], o[9], o[10], o[11], o[12], o[13], o[14], o[15]);
  and and_2 (ng, o[15], 1'b1);
  not not_4 (zr, or_1_out);

  // Notes on the sheet:
  //   x1
  //   y1
  //   notX1
  //   noty1
  //   x2
  //   y2
  //   x2 And y2
  //   x2+y2
  //   tempOut
  //   notTempOut
  //   out1
  //   zr
endmodule

module Bit (
  input  i,
  input  load,
  output o
);

  wire clock_1_out, multiplexer_1_out;

  Clock clock_1 (.out(clock_1_out));
  D_Flip_Flop d_ff_1 (.clk(clock_1_out), .D(multiplexer_1_out), .Q(o));  // open: Qn, preset, reset
  Multiplexer multiplexer_1 (.in0(o), .in1(i), .out(multiplexer_1_out), .sel(load));

  // Notes on the sheet:
  //   out1
  //   dIn
endmodule

module Register16 (
  input  [15:0] i,
  input  load,
  output [15:0] o
);

  Bit bit_1 (.i(i[15]), .load(load), .o(o[15]));
  Bit bit_2 (.i(i[7]), .load(load), .o(o[7]));
  Bit bit_3 (.i(i[14]), .load(load), .o(o[14]));
  Bit bit_4 (.i(i[6]), .load(load), .o(o[6]));
  Bit bit_5 (.i(i[13]), .load(load), .o(o[13]));
  Bit bit_6 (.i(i[5]), .load(load), .o(o[5]));
  Bit bit_7 (.i(i[12]), .load(load), .o(o[12]));
  Bit bit_8 (.i(i[4]), .load(load), .o(o[4]));
  Bit bit_9 (.i(i[11]), .load(load), .o(o[11]));
  Bit bit_10 (.i(i[3]), .load(load), .o(o[3]));
  Bit bit_11 (.i(i[10]), .load(load), .o(o[10]));
  Bit bit_12 (.i(i[2]), .load(load), .o(o[2]));
  Bit bit_13 (.i(i[9]), .load(load), .o(o[9]));
  Bit bit_14 (.i(i[1]), .load(load), .o(o[1]));
  Bit bit_15 (.i(i[8]), .load(load), .o(o[8]));
  Bit bit_16 (.i(i[0]), .load(load), .o(o[0]));
endmodule
