// Logisim project project_01.circ as structural Verilog
module Not1 (
  input  in_1,
  output out_2
);

  nand nand_1 (out_2, in_1, in_1);
endmodule

module And2 (
  input  a,
  input  b,
  output o
);

  wire nand_1_out;

  nand nand_1 (nand_1_out, a, b);
  Not1 not1_1 (.in_1(nand_1_out), .out_2(o));
endmodule

module Or3 (
  input  a,
  input  b,
  output o
);

  wire not1_1_out_2, not1_2_out_2;

  Not1 not1_1 (.in_1(a), .out_2(not1_1_out_2));
  Not1 not1_2 (.in_1(b), .out_2(not1_2_out_2));
  nand nand_1 (o, not1_1_out_2, not1_2_out_2);
endmodule

module Xor4 (
  input  a,
  input  b,
  output o
);

  wire and2_1_o, and2_2_o, not1_1_out_2, not1_2_out_2;

  Not1 not1_1 (.in_1(a), .out_2(not1_1_out_2));
  Not1 not1_2 (.in_1(b), .out_2(not1_2_out_2));
  And2 and2_1 (.a(not1_1_out_2), .b(b), .o(and2_1_o));
  And2 and2_2 (.a(not1_2_out_2), .b(a), .o(and2_2_o));
  Or3 or3_1 (.a(and2_1_o), .b(and2_2_o), .o(o));

  // Notes on the sheet:
  //   notA
  //   notB
  //   b
  //   a
  //   bnotA
  //   anotB
endmodule

module Mux5 (
  input  sel,
  input  a,
  input  b,
  output out_4
);

  wire and2_1_o, and2_2_o, not1_1_out_2;

  Not1 not1_1 (.in_1(sel), .out_2(not1_1_out_2));
  And2 and2_1 (.a(b), .b(sel), .o(and2_1_o));
  And2 and2_2 (.a(not1_1_out_2), .b(a), .o(and2_2_o));
  Or3 or3_1 (.a(and2_2_o), .b(and2_1_o), .o(out_4));

  // Notes on the sheet:
  //   notSel
  //   aSel
  //   anotSel
endmodule

module DMux6 (
  input  sel,
  input  i,
  output a,
  output b
);

  wire not1_1_out_2;

  Not1 not1_1 (.in_1(sel), .out_2(not1_1_out_2));
  And2 and2_1 (.a(not1_1_out_2), .b(i), .o(a));
  And2 and2_2 (.a(sel), .b(i), .o(b));
endmodule

module Not7_16 (
  input  [15:0] i,
  output [15:0] o
);

  Not1 not1_1 (.in_1(i[0]), .out_2(o[0]));
  Not1 not1_2 (.in_1(i[1]), .out_2(o[1]));
  Not1 not1_3 (.in_1(i[2]), .out_2(o[2]));
  Not1 not1_4 (.in_1(i[3]), .out_2(o[3]));
  Not1 not1_5 (.in_1(i[4]), .out_2(o[4]));
  Not1 not1_6 (.in_1(i[5]), .out_2(o[5]));
  Not1 not1_7 (.in_1(i[6]), .out_2(o[6]));
  Not1 not1_8 (.in_1(i[7]), .out_2(o[7]));
  Not1 not1_9 (.in_1(i[8]), .out_2(o[8]));
  Not1 not1_10 (.in_1(i[9]), .out_2(o[9]));
  Not1 not1_11 (.in_1(i[10]), .out_2(o[10]));
  Not1 not1_12 (.in_1(i[11]), .out_2(o[11]));
  Not1 not1_13 (.in_1(i[12]), .out_2(o[12]));
  Not1 not1_14 (.in_1(i[13]), .out_2(o[13]));
  Not1 not1_15 (.in_1(i[14]), .out_2(o[14]));
  Not1 not1_16 (.in_1(i[15]), .out_2(o[15]));
endmodule

module And8_16 (
  input  [15:0] a,
  input  [15:0] b,
  output [15:0] o
);

  And2 and2_1 (.a(a[0]), .b(b[0]), .o(o[0]));
  And2 and2_2 (.a(a[1]), .b(b[1]), .o(o[1]));
  And2 and2_3 (.a(a[2]), .b(b[2]), .o(o[2]));
  And2 and2_4 (.a(a[3]), .b(b[3]), .o(o[3]));
  And2 and2_5 (.a(a[4]), .b(b[4]), .o(o[4]));
  And2 and2_6 (.a(a[5]), .b(b[5]), .o(o[5]));
  And2 and2_7 (.a(a[6]), .b(b[6]), .o(o[6]));
  And2 and2_8 (.a(a[7]), .b(b[7]), .o(o[7]));
  And2 and2_9 (.a(a[8]), .b(b[8]), .o(o[8]));
  And2 and2_10 (.a(a[9]), .b(b[9]), .o(o[9]));
  And2 and2_11 (.a(a[10]), .b(b[10]), .o(o[10]));
  And2 and2_12 (.a(a[11]), .b(b[11]), .o(o[11]));
  And2 and2_13 (.a(a[12]), .b(b[12]), .o(o[12]));
  And2 and2_14 (.a(a[13]), .b(b[13]), .o(o[13]));
  And2 and2_15 (.a(a[14]), .b(b[14]), .o(o[14]));
  And2 and2_16 (.a(a[15]), .b(b[15]), .o(o[15]));
endmodule

module Or9_16 (
  input  [15:0] a,
  input  [15:0] b,
  output [15:0] o
);

  Or3 or3_1 (.a(a[0]), .b(b[0]), .o(o[0]));
  Or3 or3_2 (.a(a[1]), .b(b[1]), .o(o[1]));
  Or3 or3_3 (.a(a[2]), .b(b[2]), .o(o[2]));
  Or3 or3_4 (.a(a[3]), .b(b[3]), .o(o[3]));
  Or3 or3_5 (.a(a[4]), .b(b[4]), .o(o[4]));
  Or3 or3_6 (.a(a[5]), .b(b[5]), .o(o[5]));
  Or3 or3_7 (.a(a[6]), .b(b[6]), .o(o[6]));
  Or3 or3_8 (.a(a[7]), .b(b[7]), .o(o[7]));
  Or3 or3_9 (.a(a[8]), .b(b[8]), .o(o[8]));
  Or3 or3_10 (.a(a[9]), .b(b[9]), .o(o[9]));
  Or3 or3_11 (.a(a[10]), .b(b[10]), .o(o[10]));
  Or3 or3_12 (.a(a[11]), .b(b[11]), .o(o[11]));
  Or3 or3_13 (.a(a[12]), .b(b[12]), .o(o[12]));
  Or3 or3_14 (.a(a[13]), .b(b[13]), .o(o[13]));
  Or3 or3_15 (.a(a[14]), .b(b[14]), .o(o[14]));
  Or3 or3_16 (.a(a[15]), .b(b[15]), .o(o[15]));
endmodule

module Mux10_16 (
  input  sel,
  input  [15:0] a,
  input  [15:0] b,
  output [15:0] o
);

  Mux5 mux5_1 (.sel(sel), .a(a[0]), .b(b[0]), .out_4(o[0]));
  Mux5 mux5_2 (.sel(sel), .a(a[1]), .b(b[1]), .out_4(o[1]));
  Mux5 mux5_3 (.sel(sel), .a(a[2]), .b(b[2]), .out_4(o[2]));
  Mux5 mux5_4 (.sel(sel), .a(a[3]), .b(b[3]), .out_4(o[3]));
  Mux5 mux5_5 (.sel(sel), .a(a[4]), .b(b[4]), .out_4(o[4]));
  Mux5 mux5_6 (.sel(sel), .a(a[5]), .b(b[5]), .out_4(o[5]));
  Mux5 mux5_7 (.sel(sel), .a(a[6]), .b(b[6]), .out_4(o[6]));
  Mux5 mux5_8 (.sel(sel), .a(a[7]), .b(b[7]), .out_4(o[7]));
  Mux5 mux5_9 (.sel(sel), .a(a[8]), .b(b[8]), .out_4(o[8]));
  Mux5 mux5_10 (.sel(sel), .a(a[9]), .b(b[9]), .out_4(o[9]));
  Mux5 mux5_11 (.sel(sel), .a(a[10]), .b(b[10]), .out_4(o[10]));
  Mux5 mux5_12 (.sel(sel), .a(a[11]), .b(b[11]), .out_4(o[11]));
  Mux5 mux5_13 (.sel(sel), .a(a[12]), .b(b[12]), .out_4(o[12]));
  Mux5 mux5_14 (.sel(sel), .a(a[13]), .b(b[13]), .out_4(o[13]));
  Mux5 mux5_15 (.sel(sel), .a(a[14]), .b(b[14]), .out_4(o[14]));
  Mux5 mux5_16 (.sel(sel), .a(a[15]), .b(b[15]), .out_4(o[15]));
endmodule

module Or11_8Way (
  input  [7:0] i,
  output o
);

  wire or3_1_o, or3_2_o, or3_3_o, or3_4_o, or3_5_o, or3_6_o;

  Or3 or3_1 (.a(i[0]), .b(i[1]), .o(or3_1_o));
  Or3 or3_2 (.a(or3_1_o), .b(i[2]), .o(or3_2_o));
  Or3 or3_3 (.a(or3_2_o), .b(i[3]), .o(or3_3_o));
  Or3 or3_4 (.a(or3_3_o), .b(i[4]), .o(or3_4_o));
  Or3 or3_5 (.a(or3_4_o), .b(i[5]), .o(or3_5_o));
  Or3 or3_6 (.a(or3_5_o), .b(i[6]), .o(or3_6_o));
  Or3 or3_7 (.a(or3_6_o), .b(i[7]), .o(o));
endmodule

module Mux12_4Way16 (
  input  [1:0] sel,
  input  [15:0] a,
  input  [15:0] b,
  input  [15:0] c,
  input  [15:0] d,
  output [15:0] o
);

  wire [15:0] mux10_16_1_o, mux10_16_2_o;

  Mux10_16 mux10_16_1 (.sel(sel[0]), .a(a), .b(b), .o(mux10_16_1_o));
  Mux10_16 mux10_16_2 (.sel(sel[0]), .a(c), .b(d), .o(mux10_16_2_o));
  Mux10_16 mux10_16_3 (.sel(sel[1]), .a(mux10_16_1_o), .b(mux10_16_2_o), .o(o));
endmodule
