// Logisim project project_02.circ as structural Verilog: 1 circuit, main circuit ALU
module ALU (
  input  [15:0] x,
  input  zx,
  input  nx,
  input  f,
  input  no,
  input  [15:0] y,
  input  zy,
  input  ny,
  output zr,
  output [15:0] o,
  output ng
);

  wire or_1_out;
  wire [15:0] adder_1_out, and_1_out, multiplexer_1_out, multiplexer_2_out, multiplexer_3_out,
       multiplexer_4_out, multiplexer_5_out, not_1_out, not_2_out, not_3_out;

  Multiplexer #(.width(16)) multiplexer_1 (.in0(x), .in1({16{1'b0}}), .out(multiplexer_1_out), .sel(zx));
  Multiplexer #(.width(16)) multiplexer_2 (.in0(y), .in1({16{1'b0}}), .out(multiplexer_2_out), .sel(zy));
  assign not_1_out = ~multiplexer_2_out;  // NOT_Gate not_1, 16 bits wide
  assign not_2_out = ~multiplexer_1_out;  // NOT_Gate not_2, 16 bits wide
  Multiplexer #(.width(16)) multiplexer_3 (.in0(multiplexer_2_out), .in1(not_1_out), .out(multiplexer_3_out), .sel(ny));
  Multiplexer #(.width(16)) multiplexer_4 (.in0(multiplexer_1_out), .in1(not_2_out), .out(multiplexer_4_out), .sel(nx));
  assign and_1_out = multiplexer_4_out & multiplexer_3_out;  // AND_Gate and_1, 16 bits wide
  Adder #(.width(16)) adder_1 (.a(multiplexer_4_out), .b(multiplexer_3_out), .out(adder_1_out));  // open: cin, cout
  Multiplexer #(.width(16)) multiplexer_5 (.in0(and_1_out), .in1(adder_1_out), .out(multiplexer_5_out), .sel(f));
  assign not_3_out = ~multiplexer_5_out;  // NOT_Gate not_3, 16 bits wide
  Multiplexer #(.width(16)) multiplexer_6 (.in0(multiplexer_5_out), .in1(not_3_out), .out(o), .sel(no));
  or or_1 (or_1_out, o[0], o[1], o[2], o[3], o[4], o[5], o[6], o[7], o[8], o[9], o[10], o[11], o[12], o[13], o[14], o[15]);
  and and_2 (ng, o[15], 1'b1);
  not not_4 (zr, or_1_out);

  // Notes on the sheet:
  //   x1
  //   y1
  //   notX1
  //   noty1
  //   x2
  //   y2
  //   x2 And y2
  //   x2+y2
  //   tempOut
  //   notTempOut
  //   out1
  //   zr
endmodule
