// Logisim project project_03.circ as structural Verilog: 6 circuits, main circuit main
module main (
);

  Bit bit_1 ();  // open: i, load, o
  Ram8 ram8_1 ();  // open: load, address, i, o
  Register16 register16_1 ();  // open: load, i, o
  PC pc_1 ();  // open: reset, load, inc, i, o
endmodule

module Bit (
  input  i,
  input  load,
  output o
);

  wire clock_1_out, multiplexer_1_out;

  Clock clock_1 (.out(clock_1_out));
  D_Flip_Flop d_ff_1 (.clk(clock_1_out), .D(multiplexer_1_out), .Q(o));  // open: Qn, preset, reset
  Multiplexer multiplexer_1 (.in0(o), .in1(i), .out(multiplexer_1_out), .sel(load));

  // Notes on the sheet:
  //   out1
  //   dIn
endmodule

module Register16 (
  input  [15:0] i,
  input  load,
  output [15:0] o
);

  Bit bit_1 (.i(i[15]), .load(load), .o(o[15]));
  Bit bit_2 (.i(i[7]), .load(load), .o(o[7]));
  Bit bit_3 (.i(i[14]), .load(load), .o(o[14]));
  Bit bit_4 (.i(i[6]), .load(load), .o(o[6]));
  Bit bit_5 (.i(i[13]), .load(load), .o(o[13]));
  Bit bit_6 (.i(i[5]), .load(load), .o(o[5]));
  Bit bit_7 (.i(i[12]), .load(load), .o(o[12]));
  Bit bit_8 (.i(i[4]), .load(load), .o(o[4]));
  Bit bit_9 (.i(i[11]), .load(load), .o(o[11]));
  Bit bit_10 (.i(i[3]), .load(load), .o(o[3]));
  Bit bit_11 (.i(i[10]), .load(load), .o(o[10]));
  Bit bit_12 (.i(i[2]), .load(load), .o(o[2]));
  Bit bit_13 (.i(i[9]), .load(load), .o(o[9]));
  Bit bit_14 (.i(i[1]), .load(load), .o(o[1]));
  Bit bit_15 (.i(i[8]), .load(load), .o(o[8]));
  Bit bit_16 (.i(i[0]), .load(load), .o(o[0]));
endmodule

module Ram8 (
  input  [15:0] i,
  input  load,
  input  [2:0] address,
  output [15:0] o
);

  wire demultiplexer_1_out0, demultiplexer_1_out1, demultiplexer_1_out2, demultiplexer_1_out3,
       demultiplexer_1_out5, demultiplexer_1_out6, demultiplexer_1_out7;
  wire [15:0] register16_1_o, register16_2_o, register16_3_o, register16_4_o, register16_5_o, register16_6_o,
       register16_7_o, register16_8_o;

  Demultiplexer #(.select(3)) demultiplexer_1 (
    .out0(demultiplexer_1_out0), .out1(demultiplexer_1_out1), .out2(demultiplexer_1_out2),
    .out3(demultiplexer_1_out3), .out4(demultiplexer_1_out3), .out5(demultiplexer_1_out5),
    .out6(demultiplexer_1_out6), .out7(demultiplexer_1_out7), .in(load), .sel(address));
  Register16 register16_1 (.load(demultiplexer_1_out7), .i(i), .o(register16_1_o));
  Register16 register16_2 (.load(demultiplexer_1_out3), .i(i), .o(register16_2_o));
  Register16 register16_3 (.load(demultiplexer_1_out6), .i(i), .o(register16_3_o));
  Register16 register16_4 (.load(demultiplexer_1_out2), .i(i), .o(register16_4_o));
  Register16 register16_5 (.load(demultiplexer_1_out5), .i(i), .o(register16_5_o));
  Register16 register16_6 (.load(demultiplexer_1_out1), .i(i), .o(register16_6_o));
  Register16 register16_7 (.load(demultiplexer_1_out3), .i(i), .o(register16_7_o));
  Register16 register16_8 (.load(demultiplexer_1_out0), .i(i), .o(register16_8_o));
  Multiplexer #(.select(3), .width(16)) multiplexer_1 (
    .in0(register16_8_o), .in1(register16_6_o), .in2(register16_4_o), .in3(register16_2_o),
    .in4(register16_7_o), .in5(register16_5_o), .in6(register16_3_o), .in7(register16_1_o), .out(o),
    .sel(address));
endmodule

module Ram64 (
  input  [15:0] i,
  input  load,
  input  [5:0] address,
  output [15:0] o
);

  wire demultiplexer_1_out0, demultiplexer_1_out1, demultiplexer_1_out2, demultiplexer_1_out3,
       demultiplexer_1_out5, demultiplexer_1_out6, demultiplexer_1_out7;
  wire [15:0] ram8_1_o, ram8_2_o, ram8_3_o, ram8_4_o, ram8_5_o, ram8_6_o, ram8_7_o, ram8_8_o;

  Demultiplexer #(.select(3)) demultiplexer_1 (
    .out0(demultiplexer_1_out0), .out1(demultiplexer_1_out1), .out2(demultiplexer_1_out2),
    .out3(demultiplexer_1_out3), .out4(demultiplexer_1_out3), .out5(demultiplexer_1_out5),
    .out6(demultiplexer_1_out6), .out7(demultiplexer_1_out7), .in(load), .sel(address[5:3]));
  Ram8 ram8_1 (.load(demultiplexer_1_out7), .address(address[2:0]), .i(i), .o(ram8_1_o));
  Ram8 ram8_2 (.load(demultiplexer_1_out3), .address(address[2:0]), .i(i), .o(ram8_2_o));
  Ram8 ram8_3 (.load(demultiplexer_1_out6), .address(address[2:0]), .i(i), .o(ram8_3_o));
  Ram8 ram8_4 (.load(demultiplexer_1_out2), .address(address[2:0]), .i(i), .o(ram8_4_o));
  Ram8 ram8_5 (.load(demultiplexer_1_out5), .address(address[2:0]), .i(i), .o(ram8_5_o));
  Ram8 ram8_6 (.load(demultiplexer_1_out1), .address(address[2:0]), .i(i), .o(ram8_6_o));
  Ram8 ram8_7 (.load(demultiplexer_1_out3), .address(address[2:0]), .i(i), .o(ram8_7_o));
  Ram8 ram8_8 (.load(demultiplexer_1_out0), .address(address[2:0]), .i(i), .o(ram8_8_o));
  Multiplexer #(.select(3), .width(16)) multiplexer_1 (
    .in0(ram8_8_o), .in1(ram8_6_o), .in2(ram8_4_o), .in3(ram8_2_o), .in4(ram8_7_o), .in5(ram8_5_o),
    .in6(ram8_3_o), .in7(ram8_1_o), .out(o), .sel(address[5:3]));
endmodule

module PC (
  input  [15:0] i,
  input  reset,
  input  load,
  input  inc,
  output [15:0] o
);

  wire and_2_out, not_1_out, not_2_out, or_1_out, or_2_out;
  wire [15:0] adder_1_out, and_3_out, and_5_out, or_3_out;
  wire [15:15] and_1_out, and_4_out;

  or or_1 (or_1_out, reset, load);
  or or_2 (or_2_out, or_1_out, inc);
  not not_1 (not_1_out, load);
  not not_2 (not_2_out, reset);
  and and_1 (and_1_out[15], not_2_out, load);
  and and_2 (and_2_out, not_2_out, not_1_out);
  Register16 register16_1 (.load(or_2_out), .i(or_3_out), .o(o));
  assign and_3_out = {16{and_1_out[15]}} & i;  // AND_Gate and_3, 16 bits wide
  and and_4 (and_4_out[15], and_2_out, inc);
  Adder #(.width(16)) adder_1 (.a(o), .b({16{1'b0}}), .out(adder_1_out), .cin(1'b1));  // open: cout
  assign and_5_out = {16{and_4_out[15]}} & adder_1_out;  // AND_Gate and_5, 16 bits wide
  assign or_3_out = and_3_out | and_5_out;  // OR_Gate or_3, 16 bits wide

  // Notes on the sheet:
  //   rl
  //   sel
  //   notLoad
  //   notReset
  //   ld
  //   nrl
  //   out1
  //   mask1
  //   inrl
  //   tempInc
  //   out2
  //   mask2
  //   out3
  //   out4
endmodule
