// Logisim project project_5.circ as structural Verilog: 3 circuits, main circuit CPU
module CPU (
  input  [15:0] i,
  input  [15:0] inM,
  input  reset,
  output [15:0] outM,
  output [14:0] addressM,
  output [14:0] pc_next,
  output writeM
);

  wire and_1_out, and_2_out, and_3_out, and_4_out, and_5_out, and_6_out, and_7_out, and_8_out, and_9_out,
       multiplexer_2_out, NgFlag, not_1_out, or_1_out, or_2_out, ZeroFlag;
  wire [15:0] multiplexer_1_out, multiplexer_3_out, register16_2_o;
  wire [15:15] pc_1_o, register16_1_o;

  not not_1 (not_1_out, i[15]);
  Multiplexer #(.width(16)) multiplexer_1 (.in0(i), .in1(outM), .out(multiplexer_1_out), .sel(i[15]));
  or or_1 (or_1_out, NgFlag, ZeroFlag);
  Multiplexer multiplexer_2 (.in0(not_1_out), .in1(i[5]), .out(multiplexer_2_out), .sel(i[15]));
  and and_1 (and_1_out, i[15], i[4]);
  Register16 register16_1 (.load(multiplexer_2_out), .i(multiplexer_1_out), .o({register16_1_o[15], addressM}));
  and and_2 (and_2_out, ~i[2], ~i[1], i[0], ~ZeroFlag, ~NgFlag);  // AND_Gate
  and and_3 (and_3_out, ~i[2], i[1], ~i[0], ZeroFlag, ~NgFlag);  // AND_Gate
  and and_4 (and_4_out, ~i[2], i[1], i[0], ~NgFlag);  // AND_Gate
  and and_5 (and_5_out, i[2], ~i[1], ~i[0], ~ZeroFlag, NgFlag);  // AND_Gate
  and and_6 (and_6_out, i[2], ~i[1], i[0], ~ZeroFlag);  // AND_Gate
  and and_7 (and_7_out, i[2], i[1], ~i[0], or_1_out);  // AND_Gate
  and and_8 (and_8_out, i[2], i[1], i[0]);
  Register16 register16_2 (.load(and_1_out), .i(outM), .o(register16_2_o));
  Multiplexer #(.width(16)) multiplexer_3 (
    .in0({register16_1_o[15], addressM}), .in1(inM), .out(multiplexer_3_out), .sel(i[12]));
  or or_2 (or_2_out, and_2_out, and_3_out, and_4_out, and_5_out, and_6_out, and_7_out, and_8_out);
  ALU alu_1 (
    .ny(i[8]), .zx(i[11]), .nx(i[10]), .f(i[7]), .no(i[6]), .zy(i[9]), .x(register16_2_o),
    .y(multiplexer_3_out), .o(outM), .zr(ZeroFlag), .ng(NgFlag));
  and and_9 (and_9_out, or_2_out, i[15]);
  PC pc_1 (.reset(reset), .load(and_9_out), .inc(1'b1), .i({register16_1_o[15], addressM}), .o({pc_1_o[15], pc_next}));
  and and_10 (writeM, i[3], i[15]);

  // Other names for the same wires on the sheet: ins0 = i[0]; ins1 = i[1]; ins2 = i[2]; ins3 = i[3]; ins4 = i[4];
  //   ins5 = i[5]; ins6 = i[6]; ins7 = i[7]; ins8 = i[8]; ins9 = i[9]; ins10 = i[10]; ins11 = i[11]; ins12 = i[12];
  //   ins13 = i[13]; ins14 = i[14]; ins15 = i[15]

  // Notes on the sheet:
  //   instruction
  //   inM
  //   ALUoutput
  //   Ainput
  //   AInsFlag
  //   AFlag
  //   A register
  //   Aout
  //   i1
  //   i2
  //   i3
  //   i4
  //   i5
  //   i6
  //   i7
  //   DFlag
  //   D register
  //   ALUinputy
  //   ALUinputx
  //   JmpFlag
  //   JmpSelect
  //   outM
  //   addressM
  //   PC
  //   writeM
endmodule

module Memory (
  input  [14:0] address,
  input  load,
  input  [15:0] i,
  input  [15:0] key,
  output [15:0] o
);

  wire and_1_out, and_2_out, and_3_out, clock_1_out, multiplexer_1_out, multiplexer_2_out, or_1_out;
  wire [15:0] multiplexer_3_out, multiplexer_4_out, multiplexer_5_out, ram_1_dout, ram_2_dout, register16_1_o;

  Clock clock_1 (.out(clock_1_out));
  Multiplexer multiplexer_1 (.in0(load), .in1(1'b0), .out(multiplexer_1_out), .sel(address[14]));
  and and_1 (and_1_out, ~address[13], address[14]);  // AND_Gate
  and and_2 (and_2_out, address[13], address[14]);
  RAM #(.addrWidth(14), .dataWidth(16)) ram_1 (
    .addr(address[13:0]), .we(multiplexer_1_out), .oe(1'b1), .clk(clock_1_out), .din(i), .dout(ram_1_dout));
  Multiplexer multiplexer_2 (.in0(1'b0), .in1(load), .out(multiplexer_2_out), .sel(and_1_out));
  or or_1 (or_1_out, address[0], address[1], address[2], address[3], address[4], address[5], address[6], address[7], address[8], address[9], address[10], address[11], address[12]);
  and and_3 (and_3_out, and_2_out, ~or_1_out);  // AND_Gate
  RAM #(.addrWidth(13), .dataWidth(16)) ram_2 (
    .addr(address[12:0]), .we(multiplexer_2_out), .oe(1'b1), .clk(clock_1_out), .din(i), .dout(ram_2_dout));
  Register16 register16_1 (.load(1'b1), .i(key), .o(register16_1_o));
  Multiplexer #(.width(16)) multiplexer_3 (
    .in0(ram_1_dout), .in1({16{1'b0}}), .out(multiplexer_3_out), .sel(address[14]));
  Multiplexer #(.width(16)) multiplexer_4 (
    .in0({16{1'b0}}), .in1(ram_2_dout), .out(multiplexer_4_out), .sel(and_1_out));
  Multiplexer #(.width(16)) multiplexer_5 (
    .in0({16{1'b0}}), .in1(register16_1_o), .out(multiplexer_5_out), .sel(and_3_out));
  assign o = multiplexer_3_out | multiplexer_4_out | multiplexer_5_out;  // OR_Gate or_2, 16 bits wide

  // Other names for the same wires on the sheet: a13 = address[13]; a0 = address[0]; a1 = address[1]; a2 = address[2];
  //   a3 = address[3]; a4 = address[4]; a5 = address[5]; a6 = address[6]; a7 = address[7]; a8 = address[8];
  //   a9 = address[9]; a10 = address[10]; a11 = address[11]; a12 = address[12]; a14 = address[14]

  // Notes on the sheet:
  //   loadRamOut
  //   flag
  //   ScrSelect
  //   keySelect1
  //   flag2
  //   RamOut1
  //   keySelect
  //   RamOut2
  //   ScreenOut
  //   Keyout
endmodule

module test_1 (
  input  reset,
  output [15:0] outM,
  output [14:0] addressM,
  output [15:0] out_4,
  output [14:0] pc_next,
  output writeM
);

  wire and_1_out, and_2_out, and_3_out, and_4_out, and_5_out, and_6_out, and_7_out, and_8_out, and_9_out,
       clock_1_out, ins0, ins1, ins2, ins3, ins4, ins5, ins6, ins7, ins8, ins9, ins10, ins11, ins12, ins13,
       ins14, ins15, multiplexer_2_out, NgFlag, not_1_out, or_1_out, or_2_out, ZeroFlag;
  wire [14:0] multiplexer_1_out_2, multiplexer_4_out;
  wire [15:0] multiplexer_3_out, register16_2_o;
  wire [15:15] multiplexer_1_out, pc_1_o, register16_1_o;

  ROM #(.addrWidth(15), .dataWidth(16)) rom_1 (
    .addr(pc_next),
    .data({ins15, ins14, ins13, ins12, ins11, ins10, ins9, ins8, ins7, ins6, ins5, ins4, ins3, ins2, ins1, ins0}));
  Multiplexer #(.width(16)) multiplexer_1 (
    .in0({ins15, ins14, ins13, ins12, ins11, ins10, ins9, ins8, ins7, ins6, ins5, ins4, ins3, ins2, ins1, ins0}),
    .in1(outM), .out({multiplexer_1_out[15], multiplexer_1_out_2}), .sel(ins15));
  not not_1 (not_1_out, ins15);
  or or_1 (or_1_out, NgFlag, ZeroFlag);
  Multiplexer multiplexer_2 (.in0(not_1_out), .in1(ins5), .out(multiplexer_2_out), .sel(ins15));
  and and_1 (and_1_out, ins15, ins4);
  and and_2 (and_2_out, ~ins2, ~ins1, ins0, ~ZeroFlag, ~NgFlag);  // AND_Gate
  and and_3 (and_3_out, ~ins2, ins1, ~ins0, ZeroFlag, ~NgFlag);  // AND_Gate
  and and_4 (and_4_out, ~ins2, ins1, ins0, ~NgFlag);  // AND_Gate
  and and_5 (and_5_out, ins2, ~ins1, ~ins0, ~ZeroFlag, NgFlag);  // AND_Gate
  and and_6 (and_6_out, ins2, ~ins1, ins0, ~ZeroFlag);  // AND_Gate
  and and_7 (and_7_out, ins2, ins1, ~ins0, or_1_out);  // AND_Gate
  and and_8 (and_8_out, ins2, ins1, ins0);
  Register16 register16_1 (
    .load(multiplexer_2_out), .i({multiplexer_1_out[15], multiplexer_1_out_2}),
    .o({register16_1_o[15], addressM}));
  Multiplexer #(.width(16)) multiplexer_3 (
    .in0({register16_1_o[15], addressM}), .in1(out_4), .out(multiplexer_3_out), .sel(ins12));
  Register16 register16_2 (.load(and_1_out), .i(outM), .o(register16_2_o));
  or or_2 (or_2_out, and_2_out, and_3_out, and_4_out, and_5_out, and_6_out, and_7_out, and_8_out);
  and and_9 (and_9_out, or_2_out, ins15);
  ALU alu_1 (
    .ny(ins8), .zx(ins11), .nx(ins10), .f(ins7), .no(ins6), .zy(ins9), .x(register16_2_o),
    .y(multiplexer_3_out), .o(outM), .zr(ZeroFlag), .ng(NgFlag));
  PC pc_1 (.reset(reset), .load(and_9_out), .inc(1'b1), .i({register16_1_o[15], addressM}), .o({pc_1_o[15], pc_next}));
  Multiplexer #(.width(15)) multiplexer_4 (
    .in0(multiplexer_1_out_2), .in1(addressM), .out(multiplexer_4_out), .sel(ins15));
  and and_10 (writeM, ins3, ins15);
  RAM #(.addrWidth(15), .dataWidth(16)) ram_1 (
    .addr(multiplexer_4_out), .we(writeM), .oe(1'b1), .clk(clock_1_out), .din(outM), .dout(out_4));
  Clock clock_1 (.out(clock_1_out));

  // Other names for the same wires on the sheet: ouyM[15:0] = out_4; pc[14:0] = pc_next

  // Notes on the sheet:
  //   contents of rom_1 (hex, n*v repeats v):
  //   2 ea88 1 fc10 10 e302 2 fc10 0 f090 2 e308 1 fc88 2 ea87 10 ea87
  //   instruction
  //   inM
  //   ALUoutput
  //   AInsFlag
  //   Ainput
  //   AFlag
  //   A register
  //   i1
  //   i2
  //   i3
  //   i4
  //   i5
  //   i6
  //   i7
  //   DFlag
  //   Aout
  //   D register
  //   ALUinputy
  //   ALUinputx
  //   JmpFlag
  //   JmpSelect
  //   outM
  //   addressM
  //   PC
  //   writeM
endmodule
