// Logisim project s2 M16002.circ as structural Verilog: 12 circuits, main circuit MAIN
module MAIN (
  input  [15:0] in_1,
  output [15:0] Adresspointer
);

  wire clock_1_out, debug_1_out_2, debug_1_out_3, debug_1_out_4, debug_1_out_5, debug_1_out_6, debug_1_out_7,
       debug_1_out_8, debug_1_out_9, debug_1_out_10, debug_1_out_11, debug_1_out_12, debug_1_out_13,
       debug_1_out_14, debug_1_out_15, debug_1_out_16, debug_1_out_17, not_1_out, s2_m16002_1_ccp,
       s2_m16002_1_ck, s2_m16002_1_ckk, s2_m16002_1_cls, s2_m16002_1_hlt, s2_m16002_1_prc, s2_m16002_1_stack,
       s2_m16002_1_str;
  wire [6:0] keyboard_1_data, s2_m16002_1_cr_7;
  wire [7:0] ram_1_out, s2_m16002_1_drain, s2_m16002_1_sp;
  wire [15:0] s2_m16002_1_out_12;

  LED led_1 (.in(debug_1_out_3));
  LED led_2 (.in(debug_1_out_2));
  LED led_3 (.in(debug_1_out_11));
  LED led_4 (.in(debug_1_out_10));
  LED led_5 (.in(debug_1_out_6));
  LED led_6 (.in(debug_1_out_5));
  LED led_7 (.in(debug_1_out_7));
  LED led_8 (.in(debug_1_out_4));
  LED led_9 (.in(debug_1_out_12));
  LED led_10 (.in(debug_1_out_13));
  LED led_11 (.in(debug_1_out_14));
  LED led_12 (.in(debug_1_out_15));
  Pull_Resistor pull_resistor_1 (.node(in_1));
  LED led_13 (.in(s2_m16002_1_hlt));
  Clock clock_1 (.out(clock_1_out));
  LED led_14 (.in(debug_1_out_8));
  LED led_15 (.in(debug_1_out_9));
  Debug debug_1 (
    .in_1(s2_m16002_1_out_12), .out_2(debug_1_out_2), .out_3(debug_1_out_3), .out_4(debug_1_out_4),
    .out_5(debug_1_out_5), .out_6(debug_1_out_6), .out_7(debug_1_out_7), .out_8(debug_1_out_8),
    .out_9(debug_1_out_9), .out_10(debug_1_out_10), .out_11(debug_1_out_11), .out_12(debug_1_out_12),
    .out_13(debug_1_out_13), .out_14(debug_1_out_14), .out_15(debug_1_out_15), .out_16(debug_1_out_16),
    .out_17(debug_1_out_17));
  LED led_16 (.in(debug_1_out_17));
  LED led_17 (.in(debug_1_out_16));
  RAM ram_1 (
    .ADRESSPOINTER(Adresspointer), .SP(s2_m16002_1_sp), .STACK(s2_m16002_1_stack), .STR(s2_m16002_1_str),
    .DRAIN(s2_m16002_1_drain), .OUT(ram_1_out), .CK(s2_m16002_1_ck));
  s2_M16002 s2_m16002_1 (
    .OPCODE(in_1[15:11]), .DATA(in_1[7:0]), .DR(in_1[10:8]), .CLK(clock_1_out), .STR(s2_m16002_1_str),
    .ADRESSPOINTER(Adresspointer), .RAM(ram_1_out), .DRAIN(s2_m16002_1_drain), .ASCII_IN(keyboard_1_data),
    .CR_7(s2_m16002_1_cr_7), .PRC(s2_m16002_1_prc), .CLS(s2_m16002_1_cls), .CCP(s2_m16002_1_ccp),
    .HLT(s2_m16002_1_hlt), .CKK(s2_m16002_1_ckk), .SP(s2_m16002_1_sp), .CK(s2_m16002_1_ck),
    .STACK(s2_m16002_1_stack), .out_12(s2_m16002_1_out_12));  // open: RDC
  TTY tty_1 (.data(s2_m16002_1_cr_7), .clk(s2_m16002_1_ckk), .we(s2_m16002_1_prc), .clr(s2_m16002_1_cls));
  Keyboard keyboard_1 (.clk(not_1_out), .clr(s2_m16002_1_ccp), .data(keyboard_1_data));  // open: re, avail
  not not_1 (not_1_out, s2_m16002_1_ck);
endmodule

module s2_M16002 (
  input  [7:0] RAM,
  input  [6:0] ASCII_IN,
  input  [4:0] OPCODE,
  input  [7:0] DATA,
  input  [2:0] DR,
  input  CLK,
  output STACK,
  output [7:0] SP,
  output STR,
  output [15:0] ADRESSPOINTER,
  output [7:0] DRAIN,
  output [15:0] out_12,
  output [6:0] CR_7,
  output RDC,
  output CKK,
  output CK,
  output PRC,
  output CLS,
  output HLT,
  output CCP
);

  wire alu_1_alu_fkt, alu_1_borrow_out, alu_1_carry_out, decoder_1_out1, decoder_1_out2, decoder_1_out3,
       decoder_1_out4, decoder_1_out5, decoder_1_out6, decoder_1_out7, decoder_1_out8, decoder_1_out9,
       decoder_1_out10, decoder_1_out11, decoder_1_out12, decoder_1_out13, decoder_1_out14, decoder_1_out15,
       decoder_1_out16, decoder_1_out17, decoder_1_out18, decoder_1_out19, decoder_1_out20, decoder_1_out21,
       decoder_1_out22, decoder_1_out23, decoder_1_out24, decoder_1_out31, flagregister_1_jmp_2, not_1_out,
       or_6_out, register_1_rhlt;
  wire [2:0] or_3_out;
  wire [4:0] or_1_out;
  wire [6:0] bit_extender_1_out, bit_extender_2_out;
  wire [7:0] alu_1_out, flagregister_1_fr, or_2_out, pull_resistor_1_node, register_1_a, register_1_cp,
       register_1_h, register_1_source_2, register_1_x;

  Pull_Resistor pull_resistor_1 (.node(pull_resistor_1_node));
  Decoder #(.select(5), .enable("false")) decoder_1 (
    .out1(decoder_1_out1), .out2(decoder_1_out2), .out3(decoder_1_out3), .out4(decoder_1_out4),
    .out5(decoder_1_out5), .out6(decoder_1_out6), .out7(decoder_1_out7), .out8(decoder_1_out8),
    .out9(decoder_1_out9), .out10(decoder_1_out10), .out11(decoder_1_out11), .out12(decoder_1_out12),
    .out13(decoder_1_out13), .out14(decoder_1_out14), .out15(decoder_1_out15), .out16(decoder_1_out16),
    .out17(decoder_1_out17), .out18(decoder_1_out18), .out19(decoder_1_out19), .out20(decoder_1_out20),
    .out21(decoder_1_out21), .out22(decoder_1_out22), .out23(decoder_1_out23), .out24(decoder_1_out24),
    .out27(RDC), .out28(PRC), .out29(CLS), .out30(CCP), .out31(decoder_1_out31), .sel(or_1_out));  // open: out0, out25, out26
  assign or_1_out = OPCODE | out_12[15:11];  // OR_Gate or_1, 5 bits wide
  assign or_2_out = DATA | out_12[7:0];  // OR_Gate or_2, 8 bits wide
  assign or_3_out = DR | out_12[10:8];  // OR_Gate or_3, 3 bits wide
  Pull_Resistor pull_resistor_2 (.node(out_12));
  ROM #(.dataWidth(16)) rom_1 (.addr(pull_resistor_1_node), .data(out_12));  // open: sel
  and and_1 (CK, CLK, not_1_out);
  REGISTER register_1 (
    .JMP(flagregister_1_jmp_2), .MOV(decoder_1_out1), .MOC(decoder_1_out2), .ALU(alu_1_alu_fkt),
    .LOR(decoder_1_out17), .PUSH(decoder_1_out18), .POP(decoder_1_out19), .RDC(RDC), .Drain(or_3_out),
    .Source(or_2_out[7:5]), .DATA(or_2_out), .ALU_2(alu_1_out), .RAM(RAM), .A(register_1_a),
    .X(register_1_x), .H(register_1_h), .SP(SP), .PC(pull_resistor_1_node), .CP(register_1_cp),
    .ASCII(ASCII_IN), .ADRESS_POINTER(ADRESSPOINTER), .RHLT(register_1_rhlt), .CK(CK),
    .FR(flagregister_1_fr), .DRAIN_2(DRAIN), .SOURCE_2(register_1_source_2), .CCP(CCP));
  FlagRegister flagregister_1 (
    .RHLT(register_1_rhlt), .RDC(RDC), .carry(alu_1_carry_out), .borrow(alu_1_borrow_out),
    .ALU_FKT(alu_1_alu_fkt), .ALU(alu_1_out), .CMP(decoder_1_out14), .CMC(decoder_1_out15), .DRAIN(DRAIN),
    .SOURCE(register_1_source_2), .DATA(or_2_out), .JMP(decoder_1_out20), .JE(decoder_1_out21),
    .JNE(decoder_1_out22), .JB(decoder_1_out23), .JS(decoder_1_out24), .FR(flagregister_1_fr),
    .JMP_2(flagregister_1_jmp_2), .HLT(HLT));
  not not_1 (not_1_out, HLT);
  ALU alu_1 (
    .XNOR(decoder_1_out13), .XOR(decoder_1_out12), .NOT(decoder_1_out11), .NAND(decoder_1_out10),
    .AND(decoder_1_out9), .DIV(decoder_1_out8), .MUL(decoder_1_out7), .SUC(decoder_1_out6),
    .SUB(decoder_1_out5), .ADC(decoder_1_out4), .ADD(decoder_1_out3), .DRAIN(DRAIN),
    .SOURCE(register_1_source_2), .CONSTANT(or_2_out), .CARRY_OUT(alu_1_carry_out),
    .BORROW_OUT(alu_1_borrow_out), .OUT(alu_1_out), .ALU_FKT(alu_1_alu_fkt), .OR(decoder_1_out31));
  Bit_Extender #(.out_width(7)) bit_extender_1 (.in(DRAIN), .out(bit_extender_1_out));
  or or_4 (STACK, decoder_1_out18, decoder_1_out19);
  or or_5 (STR, decoder_1_out18, decoder_1_out16);
  Bit_Extender #(.out_width(7)) bit_extender_2 (.in(or_2_out), .out(bit_extender_2_out));
  or or_6 (or_6_out, bit_extender_2_out[0], bit_extender_2_out[1], bit_extender_2_out[2], bit_extender_2_out[3], bit_extender_2_out[4], bit_extender_2_out[5], bit_extender_2_out[6]);
  Multiplexer #(.width(7)) multiplexer_1 (
    .in0(bit_extender_1_out), .in1(bit_extender_2_out), .out(CR_7), .sel(or_6_out), .en(PRC));

  assign CKK = CK;

  // Notes on the sheet:
  //   contents of rom_1 (hex, n*v repeats v):
  //   0 13ff 1100 12ff 8800 900 1200 0 e073 e03a e05c e03e e020 100a 0 d800 e500 9500 7500 b00e 0 9800 0
  //   9800 7870 a81b a03f 0 9800 786c a820 a03f 0 9800 7865 a825 a03f 0 9800 7868 a82a a03f 0 e020 e020
  //   e063 e06c e073 e00a e020 e020 e06e e065 e077 e00a e020 e020 e06f e070 e065 e06e e00a a000 0 13fc
  //   9800 7873 a845 a052 0 9800 786c a84a a052 0 9800 7863 a84f a052 0 e800 a000 0 13fc 9800 7877 a858
  //   a084 0 9800 7865 a85d a084 0 9800 786e a862 a084 0 e800 e04e e061 e06d e065 e03a e020 d800 e500 e00a
  //   1023 8000 1001 1820 900 8500 0 1001 1820 900 d800 e500 8500 7d23 a87d a073 0 e800 820 1100 12ff 8000
  //   a000 0 13fb 9800 786e a88a a000 0 9800 7865 a88f a000 0 9800 7870 a894 a000 0 9800 786f a899 a000 0
  //   e800 e04e e061 e06d e065 e03a e020 d800 e500 1100 0 8800 7823 a8b3 79ff a8ab a0ae 0 e00a a000 0 1001
  //   1820 900 a0a4 0 1001 1820 900 8800 70a0 a8bb a0a4 0 e00a 0 1001 1820 900 8d00 7d23 a8c6 e500 a0bd 0
  //   e00a a000
endmodule

module RAM (
  input  [15:0] ADRESSPOINTER,
  input  [7:0] SP,
  input  STACK,
  input  STR,
  input  [7:0] DRAIN,
  input  CK,
  output [7:0] OUT
);

  wire adder_1_cout, buffer_1_out, buffer_2_out, buffer_3_out, buffer_4_out, buffer_5_out, buffer_6_out,
       buffer_7_out, buffer_8_out, buffer_9_out, buffer_10_out, pull_resistor_1_node, pull_resistor_3_node,
       pull_resistor_4_node, pull_resistor_5_node;
  wire [7:0] pull_resistor_2_node;
  wire [15:0] adder_1_out, multiplexer_1_out;
  wire [16:16] and_1_out;

  Pull_Resistor #(.pull(1)) pull_resistor_1 (.node(pull_resistor_1_node));
  Adder #(.width(16)) adder_1 (
    .a(16'hff), .b(ADRESSPOINTER), .out(adder_1_out), .cin(pull_resistor_1_node), .cout(adder_1_cout));
  Pull_Resistor pull_resistor_2 (.node(pull_resistor_2_node));
  Multiplexer #(.width(16), .enable("false")) multiplexer_1 (
    .in0(adder_1_out), .in1({pull_resistor_2_node, SP}), .out(multiplexer_1_out), .sel(STACK));
  and and_1 (and_1_out[16], STACK, adder_1_cout);
  Pull_Resistor #(.pull(1)) pull_resistor_3 (.node(pull_resistor_3_node));
  buf buffer_1 (buffer_1_out, buffer_2_out);
  Pull_Resistor #(.pull(1)) pull_resistor_4 (.node(pull_resistor_4_node));
  buf buffer_2 (buffer_2_out, buffer_3_out);
  buf buffer_3 (buffer_3_out, buffer_4_out);
  buf buffer_4 (buffer_4_out, buffer_5_out);
  buf buffer_5 (buffer_5_out, buffer_6_out);
  buf buffer_6 (buffer_6_out, buffer_7_out);
  buf buffer_7 (buffer_7_out, buffer_8_out);
  buf buffer_8 (buffer_8_out, buffer_9_out);
  buf buffer_9 (buffer_9_out, buffer_10_out);
  buf buffer_10 (buffer_10_out, CK);
  RAM_part #(.addrWidth(17), .bus("separate")) ram_1 (
    .addr({and_1_out[16], multiplexer_1_out}), .din(DRAIN), .data(OUT), .str(STR),
    .sel(pull_resistor_4_node), .clk(buffer_1_out), .ld(pull_resistor_3_node), .clr(pull_resistor_5_node));
  Pull_Resistor pull_resistor_5 (.node(pull_resistor_5_node));
endmodule

module ALU (
  input  OR,
  input  XNOR,
  input  XOR,
  input  NOT,
  input  NAND,
  input  AND,
  input  DIV,
  input  MUL,
  input  SUC,
  input  SUB,
  input  ADC,
  input  ADD,
  input  [7:0] DRAIN,
  input  [7:0] SOURCE,
  input  [7:0] CONSTANT,
  output [7:0] OUT,
  output ALU_FKT,
  output CARRY_OUT,
  output BORROW_OUT
);

  wire adder_1_cout, adder_2_cout, or_2_out, subtractor_1_bout, subtractor_2_bout;
  wire [7:0] adder_1_out, adder_2_out, and_1_out, divider_1_out, multiplier_1_out, nand_1_out, not_1_out,
       or_3_out, or_5_out, pull_resistor_4_node, pull_resistor_5_node, pull_resistor_6_node,
       pull_resistor_7_node, pull_resistor_8_node, pull_resistor_9_node, pull_resistor_10_node,
       pull_resistor_11_node, pull_resistor_12_node, pull_resistor_13_node, pull_resistor_14_node,
       pull_resistor_15_node, subtractor_1_out, subtractor_2_out, xnor_1_out, xor_1_out;

  or or_1 (ALU_FKT, OR, or_2_out);
  or or_2 (or_2_out, XNOR, XOR, NOT, NAND, AND, DIV, MUL, SUC, SUB, ADC, ADD);
  Pull_Resistor pull_resistor_1 (.node(DRAIN));
  Pull_Resistor pull_resistor_2 (.node(SOURCE));
  Pull_Resistor pull_resistor_3 (.node(CONSTANT));
  Pull_Resistor pull_resistor_4 (.node(pull_resistor_4_node));
  assign pull_resistor_4_node = ADD ? adder_1_out : 8'bz;  // Controlled_Buffer controlled_buffer_1
  Adder adder_1 (.a(DRAIN), .b(SOURCE), .out(adder_1_out), .cout(adder_1_cout));  // open: cin
  Adder adder_2 (.a(DRAIN), .b(CONSTANT), .out(adder_2_out), .cout(adder_2_cout));  // open: cin
  Subtractor subtractor_1 (.a(DRAIN), .b(SOURCE), .out(subtractor_1_out), .bout(subtractor_1_bout));  // open: bin
  Subtractor subtractor_2 (.a(DRAIN), .b(CONSTANT), .out(subtractor_2_out), .bout(subtractor_2_bout));  // open: bin
  Multiplier multiplier_1 (.a(DRAIN), .b(SOURCE), .out(multiplier_1_out));  // open: cin, cout
  Divider divider_1 (.a(DRAIN), .b(SOURCE), .out(divider_1_out));  // open: upper, rem
  assign and_1_out = DRAIN & SOURCE;  // AND_Gate and_1, 8 bits wide
  assign nand_1_out = ~(DRAIN & SOURCE);  // NAND_Gate nand_1, 8 bits wide
  assign not_1_out = ~DRAIN;  // NOT_Gate not_1, 8 bits wide
  assign xor_1_out = DRAIN ^ SOURCE;  // XOR_Gate xor_1, 8 bits wide
  assign xnor_1_out = ~(DRAIN ^ SOURCE);  // XNOR_Gate xnor_1, 8 bits wide
  assign or_3_out = SOURCE | DRAIN;  // OR_Gate or_3, 8 bits wide
  Pull_Resistor pull_resistor_5 (.node(pull_resistor_5_node));
  Pull_Resistor pull_resistor_6 (.node(pull_resistor_6_node));
  assign pull_resistor_6_node = SUB ? subtractor_1_out : 8'bz;  // Controlled_Buffer controlled_buffer_2
  assign pull_resistor_5_node = ADC ? adder_2_out : 8'bz;  // Controlled_Buffer controlled_buffer_3
  assign OUT = or_5_out | pull_resistor_10_node;  // OR_Gate or_4, 8 bits wide
  assign or_5_out = pull_resistor_4_node | pull_resistor_5_node | pull_resistor_6_node | pull_resistor_7_node | pull_resistor_8_node | pull_resistor_9_node | pull_resistor_13_node | pull_resistor_12_node | pull_resistor_11_node | pull_resistor_15_node | pull_resistor_14_node;  // OR_Gate or_5, 8 bits wide
  Pull_Resistor pull_resistor_7 (.node(pull_resistor_7_node));
  Pull_Resistor pull_resistor_8 (.node(pull_resistor_8_node));
  Pull_Resistor pull_resistor_9 (.node(pull_resistor_9_node));
  assign pull_resistor_9_node = DIV ? divider_1_out : 8'bz;  // Controlled_Buffer controlled_buffer_4
  assign pull_resistor_8_node = MUL ? multiplier_1_out : 8'bz;  // Controlled_Buffer controlled_buffer_5
  assign pull_resistor_7_node = SUC ? subtractor_2_out : 8'bz;  // Controlled_Buffer controlled_buffer_6
  Pull_Resistor pull_resistor_10 (.node(pull_resistor_10_node));
  assign pull_resistor_10_node = OR ? or_3_out : 8'bz;  // Controlled_Buffer controlled_buffer_7
  Pull_Resistor pull_resistor_11 (.node(pull_resistor_11_node));
  assign pull_resistor_11_node = NOT ? not_1_out : 8'bz;  // Controlled_Buffer controlled_buffer_8
  Pull_Resistor pull_resistor_12 (.node(pull_resistor_12_node));
  assign pull_resistor_12_node = NAND ? nand_1_out : 8'bz;  // Controlled_Buffer controlled_buffer_9
  Pull_Resistor pull_resistor_13 (.node(pull_resistor_13_node));
  assign pull_resistor_13_node = AND ? and_1_out : 8'bz;  // Controlled_Buffer controlled_buffer_10
  Pull_Resistor pull_resistor_14 (.node(pull_resistor_14_node));
  assign pull_resistor_14_node = XNOR ? xnor_1_out : 8'bz;  // Controlled_Buffer controlled_buffer_11
  Pull_Resistor pull_resistor_15 (.node(pull_resistor_15_node));
  assign pull_resistor_15_node = XOR ? xor_1_out : 8'bz;  // Controlled_Buffer controlled_buffer_12
  or or_6 (CARRY_OUT, adder_1_cout, adder_2_cout);
  or or_7 (BORROW_OUT, subtractor_1_bout, subtractor_2_bout);
endmodule

module REGISTER (
  input  JMP,
  input  MOV,
  input  MOC,
  input  ALU,
  input  LOR,
  input  [6:0] ASCII,
  input  PUSH,
  input  POP,
  input  RDC,
  input  [2:0] Drain,
  input  [2:0] Source,
  input  [7:0] DATA,
  input  [7:0] ALU_2,
  input  [7:0] RAM,
  input  CCP,
  input  CK,
  input  [7:0] FR,
  output [7:0] A,
  output [15:0] ADRESS_POINTER,
  output RHLT,
  output [7:0] X,
  output [7:0] H,
  output [7:0] SP,
  output [7:0] PC,
  output [7:0] CP,
  output [7:0] DRAIN_2,
  output [7:0] SOURCE_2
);

  wire and_1_out, decoder_1_out0, decoder_1_out1, decoder_1_out2, decoder_1_out3, decoder_1_out4,
       decoder_1_out5, decoder_1_out6, not_1_out, or_1_out, or_2_out, or_3_out, or_4_out, or_5_out, or_6_out,
       pull_resistor_1_node, pull_resistor_2_node, SP_pop_done;
  wire [7:0] B_q, controlled_buffer_1_out;

  or or_1 (or_1_out, MOC, JMP);
  or or_2 (or_2_out, POP, LOR);
  assign controlled_buffer_1_out = or_1_out ? DATA : 8'bz;  // Controlled_Buffer controlled_buffer_1
  assign controlled_buffer_1_out = ALU ? ALU_2 : 8'bz;  // Controlled_Buffer controlled_buffer_2
  assign controlled_buffer_1_out = or_2_out ? RAM : 8'bz;  // Controlled_Buffer controlled_buffer_3
  or or_3 (or_3_out, MOV, MOC);
  or or_4 (or_4_out, POP, LOR, or_3_out);
  Decoder #(.select(3), .disabled(0)) decoder_1 (
    .out0(decoder_1_out0), .out1(decoder_1_out1), .out2(decoder_1_out2), .out3(decoder_1_out3),
    .out4(decoder_1_out4), .out5(decoder_1_out5), .out6(decoder_1_out6), .sel(Drain), .en(or_4_out));  // open: out7
  not not_1 (not_1_out, POP);
  Pull_Resistor pull_resistor_1 (.node(pull_resistor_1_node));
  or or_5 (or_5_out, decoder_1_out0, ALU);
  Pull_Resistor pull_resistor_2 (.node(pull_resistor_2_node));
  and and_1 (and_1_out, not_1_out, CK);
  Register B (.D(controlled_buffer_1_out), .en(decoder_1_out6), .Q(B_q), .clk(or_6_out), .clr(pull_resistor_1_node));
  Register u_A (.D(controlled_buffer_1_out), .en(or_5_out), .Q(A), .clk(or_6_out), .clr(pull_resistor_2_node));
  X___H X_H (
    .DATA(controlled_buffer_1_out), .X_enable(decoder_1_out1), .H_enable(decoder_1_out2), .X(X),
    .ADRESSPOINTER(ADRESS_POINTER), .H(H), .CK(or_6_out));
  SP u_SP (
    .enable(decoder_1_out3), .PUSH(PUSH), .POP(POP), .Data(controlled_buffer_1_out), .OUT(SP),
    .POP_done(SP_pop_done), .CK(or_6_out));
  PC u_PC (.DATA(controlled_buffer_1_out), .enable(decoder_1_out4), .JUMP(JMP), .OUT(PC), .CK(or_6_out));
  CHARBUFFER CR (
    .DATA(controlled_buffer_1_out), .enable(decoder_1_out5), .getch(RDC), .ASCII(ASCII), .OUT(CP),
    .RETURN_FROM_HLT(RHLT), .CK(or_6_out), .CCP(CCP));
  or or_6 (or_6_out, and_1_out, SP_pop_done);
  Multiplexer #(.select(3), .width(8)) multiplexer_1 (
    .in0(A), .in1(X), .in2(H), .in3(SP), .in4(PC), .in5(CP), .in7(FR), .out(controlled_buffer_1_out),
    .sel(Source), .en(MOV));  // open: in6
  Multiplexer #(.select(3), .width(8), .disabled(0), .enable("false")) multiplexer_2 (
    .in0(A), .in1(X), .in2(H), .in3(SP), .in4(PC), .in5(CP), .in6(B_q), .in7(FR), .out(DRAIN_2), .sel(Drain));
  Multiplexer #(.select(3), .width(8), .disabled(0), .enable("false")) multiplexer_3 (
    .in0(A), .in1(X), .in2(H), .in3(SP), .in4(PC), .in5(CP), .in6(B_q), .in7(FR), .out(SOURCE_2), .sel(Source));
endmodule

module X___H (
  input  [7:0] DATA,
  input  X_enable,
  input  H_enable,
  input  CK,
  output [7:0] X,
  output [15:0] ADRESSPOINTER,
  output [7:0] H
);

  wire pull_resistor_1_node;

  Register u_X (.D(DATA), .en(X_enable), .Q(ADRESSPOINTER[7:0]), .clk(CK), .clr(pull_resistor_1_node));
  Register u_H (.D(DATA), .en(H_enable), .Q(ADRESSPOINTER[15:8]), .clk(CK), .clr(pull_resistor_1_node));
  Pull_Resistor pull_resistor_1 (.node(pull_resistor_1_node));

  assign H = ADRESSPOINTER[15:8];
  assign X = ADRESSPOINTER[7:0];
endmodule

module SP (
  input  enable,
  input  PUSH,
  input  POP,
  input  [7:0] Data,
  input  CK,
  output [7:0] OUT,
  output POP_done
);

  wire and_1_out, buffer_1_out, buffer_2_out, buffer_3_out, buffer_4_out, buffer_5_out, buffer_6_out,
       buffer_7_out, buffer_8_out, buffer_9_out, buffer_10_out, buffer_11_out, buffer_12_out, buffer_13_out,
       buffer_14_out, buffer_15_out, buffer_16_out, buffer_17_out, buffer_18_out, buffer_19_out,
       buffer_20_out, buffer_21_out, buffer_22_out, buffer_23_out, buffer_24_out, buffer_25_out,
       buffer_26_out, buffer_27_out, buffer_28_out, buffer_29_out, buffer_30_out, buffer_31_out,
       buffer_32_out, buffer_33_out, buffer_34_out, buffer_35_out, buffer_36_out, buffer_37_out,
       buffer_38_out, buffer_39_out, buffer_40_out, buffer_41_out, buffer_42_out, buffer_43_out,
       buffer_44_out, or_1_out, or_2_out, or_3_out, pull_resistor_1_node;

  buf buffer_1 (buffer_1_out, POP);
  buf buffer_2 (buffer_2_out, buffer_1_out);
  or or_1 (or_1_out, PUSH, enable);
  or or_2 (or_2_out, PUSH, buffer_2_out);
  or or_3 (or_3_out, buffer_2_out, and_1_out);
  Counter #(.ongoal("stay")) counter_1 (
    .load(or_1_out), .D(Data), .count(or_2_out), .Q(OUT), .clk(or_3_out), .clr(pull_resistor_1_node));  // open: carry
  Pull_Resistor pull_resistor_1 (.node(pull_resistor_1_node));
  buf buffer_3 (buffer_3_out, buffer_2_out);
  buf buffer_4 (buffer_4_out, buffer_3_out);
  buf buffer_5 (buffer_5_out, buffer_6_out);
  and and_1 (and_1_out, ~POP, CK);  // AND_Gate
  buf buffer_6 (buffer_6_out, buffer_12_out);
  buf buffer_7 (buffer_7_out, buffer_5_out);
  buf buffer_8 (buffer_8_out, buffer_10_out);
  buf buffer_9 (buffer_9_out, buffer_8_out);
  buf buffer_10 (buffer_10_out, buffer_4_out);
  buf buffer_11 (buffer_11_out, buffer_9_out);
  buf buffer_12 (buffer_12_out, buffer_13_out);
  buf buffer_13 (buffer_13_out, buffer_15_out);
  buf buffer_14 (buffer_14_out, buffer_26_out);
  buf buffer_15 (buffer_15_out, buffer_14_out);
  buf buffer_16 (buffer_16_out, buffer_18_out);
  buf buffer_17 (buffer_17_out, buffer_16_out);
  buf buffer_18 (buffer_18_out, buffer_7_out);
  buf buffer_19 (buffer_19_out, buffer_17_out);
  buf buffer_20 (buffer_20_out, buffer_23_out);
  buf buffer_21 (buffer_21_out, buffer_20_out);
  buf buffer_22 (buffer_22_out, buffer_21_out);
  buf buffer_23 (buffer_23_out, buffer_11_out);
  buf buffer_24 (buffer_24_out, buffer_25_out);
  buf buffer_25 (buffer_25_out, buffer_37_out);
  buf buffer_26 (buffer_26_out, buffer_27_out);
  buf buffer_27 (buffer_27_out, buffer_24_out);
  buf buffer_28 (buffer_28_out, buffer_31_out);
  buf buffer_29 (buffer_29_out, buffer_30_out);
  buf buffer_30 (buffer_30_out, buffer_28_out);
  buf buffer_31 (buffer_31_out, buffer_19_out);
  buf buffer_32 (buffer_32_out, buffer_35_out);
  buf buffer_33 (buffer_33_out, buffer_22_out);
  buf buffer_34 (buffer_34_out, buffer_33_out);
  buf buffer_35 (buffer_35_out, buffer_34_out);
  buf buffer_36 (buffer_36_out, buffer_39_out);
  buf buffer_37 (buffer_37_out, buffer_38_out);
  buf buffer_38 (buffer_38_out, buffer_36_out);
  buf buffer_39 (buffer_39_out, buffer_44_out);
  buf buffer_40 (buffer_40_out, buffer_43_out);
  buf buffer_41 (buffer_41_out, buffer_29_out);
  buf buffer_42 (buffer_42_out, buffer_41_out);
  buf buffer_43 (buffer_43_out, buffer_42_out);
  buf buffer_44 (buffer_44_out, buffer_32_out);
  buf buffer_45 (POP_done, buffer_40_out);
endmodule

module PC (
  input  [7:0] DATA,
  input  enable,
  input  JUMP,
  input  CK,
  output [7:0] OUT
);

  wire and_1_out, buffer_1_out, or_1_out, or_2_out, pull_resistor_2_node, pull_resistor_3_node;

  or or_1 (or_1_out, enable, JUMP);
  and and_1 (and_1_out, ~or_1_out, CK);  // AND_Gate
  Counter #(.ongoal("stay")) counter_1 (
    .load(or_1_out), .D(DATA), .count(and_1_out), .Q(OUT), .clk(or_2_out), .clr(pull_resistor_2_node));  // open: carry
  Pull_Resistor pull_resistor_1 (.node(OUT));
  Pull_Resistor pull_resistor_2 (.node(pull_resistor_2_node));
  or or_2 (or_2_out, pull_resistor_3_node, buffer_1_out);
  Pull_Resistor pull_resistor_3 (.node(pull_resistor_3_node));
  buf buffer_1 (buffer_1_out, CK);
  Pull_Resistor pull_resistor_4 (.node(CK));
endmodule

module CHARBUFFER (
  input  [7:0] DATA,
  input  enable,
  input  getch,
  input  [6:0] ASCII,
  input  CK,
  input  CCP,
  output [7:0] OUT,
  output RETURN_FROM_HLT
);

  wire and_1_out, or_1_out, or_2_out, or_3_out;
  wire [7:0] bit_extender_1_out, multiplexer_1_out;

  or or_1 (or_1_out, ASCII[6], ASCII[5], ASCII[4], ASCII[3], ASCII[2], ASCII[1], ASCII[0]);
  or or_2 (or_2_out, enable, getch);
  assign bit_extender_1_out = {{1{1'b0}}, ASCII};  // Bit_Extender bit_extender_1
  and and_1 (and_1_out, getch, or_1_out);
  buf buffer_1 (RETURN_FROM_HLT, and_1_out);
  Multiplexer #(.width(8), .disabled(0)) multiplexer_1 (
    .in0(DATA), .in1(bit_extender_1_out), .out(multiplexer_1_out), .sel(getch), .en(or_2_out));
  Register register_1 (.D(multiplexer_1_out), .en(or_2_out), .Q(OUT), .clk(or_3_out), .clr(CCP));
  or or_3 (or_3_out, RETURN_FROM_HLT, CK);
endmodule

module FlagRegister (
  input  RHLT,
  input  RDC,
  input  carry,
  input  borrow,
  input  ALU_FKT,
  input  [7:0] ALU,
  input  CMP,
  input  CMC,
  input  [7:0] DRAIN,
  input  [7:0] SOURCE,
  input  [7:0] DATA,
  input  JMP,
  input  JE,
  input  JNE,
  input  JB,
  input  JS,
  output [7:0] FR,
  output JMP_2,
  output HLT
);

  wire and_1_out, and_2_out, and_3_out, and_4_out, buffer_1_out, buffer_2_out, buffer_3_out, buffer_4_out,
       buffer_5_out, buffer_6_out, buffer_7_out, buffer_8_out, buffer_9_out, buffer_10_out, buffer_11_out,
       buffer_12_out, buffer_13_out, buffer_14_out, buffer_15_out, buffer_16_out, buffer_17_out,
       buffer_18_out, buffer_19_out, buffer_20_out, buffer_21_out, buffer_22_out, buffer_23_out,
       buffer_24_out, buffer_25_out, buffer_26_out, buffer_27_out, comparator_1_eq, comparator_1_gt,
       comparator_1_lt, comparator_2_eq, comparator_2_gt, comparator_2_lt, comparator_3_eq, equal_qn,
       multiplexer_1_out, multiplexer_2_out, multiplexer_3_out, or_1_out, or_2_out;

  Comparator #(.mode("unsigned")) comparator_1 (
    .a(DRAIN), .b(SOURCE), .gt(comparator_1_gt), .eq(comparator_1_eq), .lt(comparator_1_lt));
  Comparator #(.mode("unsigned")) comparator_2 (
    .a(DRAIN), .b(DATA), .gt(comparator_2_gt), .eq(comparator_2_eq), .lt(comparator_2_lt));
  Comparator #(.mode("unsigned")) comparator_3 (.a(ALU), .b({8{1'b0}}), .eq(comparator_3_eq));  // open: gt, lt
  or or_1 (or_1_out, CMC, CMP);
  buf buffer_1 (buffer_1_out, or_1_out);
  buf buffer_2 (buffer_2_out, buffer_1_out);
  buf buffer_3 (buffer_3_out, buffer_2_out);
  buf buffer_4 (buffer_4_out, buffer_3_out);
  buf buffer_5 (buffer_5_out, buffer_7_out);
  buf buffer_6 (buffer_6_out, buffer_5_out);
  buf buffer_7 (buffer_7_out, ALU_FKT);
  buf buffer_8 (buffer_8_out, buffer_4_out);
  buf buffer_9 (buffer_9_out, buffer_8_out);
  buf buffer_10 (buffer_10_out, buffer_9_out);
  buf buffer_11 (buffer_11_out, buffer_10_out);
  buf buffer_12 (buffer_12_out, buffer_15_out);
  buf buffer_13 (buffer_13_out, buffer_14_out);
  buf buffer_14 (buffer_14_out, buffer_6_out);
  buf buffer_15 (buffer_15_out, buffer_13_out);
  buf buffer_16 (buffer_16_out, buffer_19_out);
  buf buffer_17 (buffer_17_out, buffer_11_out);
  buf buffer_18 (buffer_18_out, buffer_16_out);
  buf buffer_19 (buffer_19_out, buffer_17_out);
  buf buffer_20 (buffer_20_out, buffer_22_out);
  buf buffer_21 (buffer_21_out, buffer_12_out);
  buf buffer_22 (buffer_22_out, buffer_21_out);
  buf buffer_23 (buffer_23_out, buffer_26_out);
  buf buffer_24 (buffer_24_out, buffer_18_out);
  buf buffer_25 (buffer_25_out, buffer_24_out);
  buf buffer_26 (buffer_26_out, buffer_25_out);
  or or_2 (or_2_out, CMP, CMC);
  buf buffer_27 (buffer_27_out, CMC);
  Multiplexer #(.disabled(0)) multiplexer_1 (
    .in0(comparator_1_eq), .in1(comparator_2_eq), .out(multiplexer_1_out), .sel(buffer_27_out), .en(or_2_out));
  Multiplexer #(.disabled(0)) multiplexer_2 (
    .in0(comparator_1_lt), .in1(comparator_2_lt), .out(multiplexer_2_out), .sel(buffer_27_out), .en(or_2_out));
  Multiplexer #(.disabled(0)) multiplexer_3 (
    .in0(comparator_1_gt), .in1(comparator_2_gt), .out(multiplexer_3_out), .sel(buffer_27_out), .en(or_2_out));
  D_Flip_Flop d_ff (.Q(FR[0]));  // open: clk, D, Qn, preset, en, reset
  D_Flip_Flop u_HLT (.Q(FR[1]), .preset(RDC), .reset(RHLT));  // open: clk, D, Qn, en
  D_Flip_Flop u_carry (.clk(ALU_FKT), .D(carry), .Q(FR[2]));  // open: Qn, preset, en, reset
  D_Flip_Flop u_borrow (.clk(ALU_FKT), .D(borrow), .Q(FR[3]));  // open: Qn, preset, en, reset
  D_Flip_Flop zero (.clk(buffer_20_out), .D(comparator_3_eq), .Q(FR[4]));  // open: Qn, preset, en, reset
  D_Flip_Flop equal (.clk(buffer_23_out), .D(multiplexer_1_out), .Q(FR[5]), .Qn(equal_qn));  // open: preset, en, reset
  D_Flip_Flop smaller (.clk(buffer_23_out), .D(multiplexer_2_out), .Q(FR[6]));  // open: Qn, preset, en, reset
  D_Flip_Flop bigger (.clk(buffer_23_out), .D(multiplexer_3_out), .Q(FR[7]));  // open: Qn, preset, en, reset
  and and_1 (and_1_out, JE, FR[5]);
  and and_2 (and_2_out, equal_qn, JNE);
  and and_3 (and_3_out, FR[6], JS);
  and and_4 (and_4_out, FR[7], JB);
  or or_3 (JMP_2, JMP, and_1_out, and_2_out, and_3_out, and_4_out);

  assign HLT = FR[1];
endmodule

module DELAY (
  input  I,
  output O
);

  wire buffer_1_out, buffer_2_out, buffer_4_out, buffer_5_out, buffer_6_out, buffer_7_out, buffer_8_out,
       buffer_9_out, buffer_10_out, buffer_11_out, buffer_12_out, buffer_13_out, buffer_14_out,
       buffer_15_out, buffer_16_out, buffer_17_out, buffer_18_out, buffer_19_out, buffer_20_out,
       buffer_21_out, buffer_22_out, buffer_23_out, buffer_24_out, buffer_25_out, buffer_26_out,
       buffer_27_out, buffer_28_out, buffer_29_out, buffer_30_out, buffer_31_out, buffer_32_out,
       buffer_33_out, buffer_34_out, buffer_35_out, buffer_36_out, buffer_37_out, buffer_38_out,
       buffer_39_out, buffer_40_out;

  buf buffer_1 (buffer_1_out, buffer_2_out);
  buf buffer_2 (buffer_2_out, I);
  buf buffer_3 (O, buffer_5_out);
  buf buffer_4 (buffer_4_out, buffer_10_out);
  buf buffer_5 (buffer_5_out, buffer_4_out);
  buf buffer_6 (buffer_6_out, buffer_1_out);
  buf buffer_7 (buffer_7_out, buffer_9_out);
  buf buffer_8 (buffer_8_out, buffer_7_out);
  buf buffer_9 (buffer_9_out, buffer_6_out);
  buf buffer_10 (buffer_10_out, buffer_13_out);
  buf buffer_11 (buffer_11_out, buffer_21_out);
  buf buffer_12 (buffer_12_out, buffer_11_out);
  buf buffer_13 (buffer_13_out, buffer_12_out);
  buf buffer_14 (buffer_14_out, buffer_16_out);
  buf buffer_15 (buffer_15_out, buffer_8_out);
  buf buffer_16 (buffer_16_out, buffer_17_out);
  buf buffer_17 (buffer_17_out, buffer_15_out);
  buf buffer_18 (buffer_18_out, buffer_20_out);
  buf buffer_19 (buffer_19_out, buffer_27_out);
  buf buffer_20 (buffer_20_out, buffer_19_out);
  buf buffer_21 (buffer_21_out, buffer_18_out);
  buf buffer_22 (buffer_22_out, buffer_14_out);
  buf buffer_23 (buffer_23_out, buffer_25_out);
  buf buffer_24 (buffer_24_out, buffer_23_out);
  buf buffer_25 (buffer_25_out, buffer_22_out);
  buf buffer_26 (buffer_26_out, buffer_37_out);
  buf buffer_27 (buffer_27_out, buffer_28_out);
  buf buffer_28 (buffer_28_out, buffer_29_out);
  buf buffer_29 (buffer_29_out, buffer_26_out);
  buf buffer_30 (buffer_30_out, buffer_31_out);
  buf buffer_31 (buffer_31_out, buffer_33_out);
  buf buffer_32 (buffer_32_out, buffer_24_out);
  buf buffer_33 (buffer_33_out, buffer_32_out);
  buf buffer_34 (buffer_34_out, buffer_40_out);
  buf buffer_35 (buffer_35_out, buffer_34_out);
  buf buffer_36 (buffer_36_out, buffer_35_out);
  buf buffer_37 (buffer_37_out, buffer_36_out);
  buf buffer_38 (buffer_38_out, buffer_30_out);
  buf buffer_39 (buffer_39_out, buffer_38_out);
  buf buffer_40 (buffer_40_out, buffer_39_out);
endmodule

module Debug (
  input  [15:0] in_1,
  output out_2,
  output out_3,
  output out_4,
  output out_5,
  output out_6,
  output out_7,
  output out_8,
  output out_9,
  output out_10,
  output out_11,
  output out_12,
  output out_13,
  output out_14,
  output out_15,
  output out_16,
  output out_17
);


  assign out_2 = in_1[15];
  assign out_3 = in_1[14];
  assign out_4 = in_1[13];
  assign out_5 = in_1[12];
  assign out_6 = in_1[11];
  assign out_7 = in_1[10];
  assign out_8 = in_1[9];
  assign out_9 = in_1[8];
  assign out_10 = in_1[7];
  assign out_11 = in_1[6];
  assign out_12 = in_1[5];
  assign out_13 = in_1[4];
  assign out_14 = in_1[3];
  assign out_15 = in_1[2];
  assign out_16 = in_1[1];
  assign out_17 = in_1[0];
endmodule
