// Logisim project test.circ as structural Verilog: 2 circuits, main circuit nand2
module nand2 (
  input  Y,
  input  X,
  output o
);

  wire transistor_1_out, transistor_4_out;

  Transistor transistor_1 (.in(o), .out(transistor_1_out), .gate(Y));
  Transistor transistor_2 (.in(transistor_1_out), .out(o), .gate(X));
  Transistor #(.\type ("n")) transistor_3 (.in(transistor_4_out), .out(o), .gate(Y));
  Transistor #(.\type ("n")) transistor_4 (.in(1'b0), .out(transistor_4_out), .gate(X));
  // also tied to VCC on the sheet: transistor_1_out

  // Notes on the sheet:
  //   Q1
  //   Q3
  //   Q4
  //   Q2
endmodule

module not2 (
);

  nand2 nand2_1 ();  // open: Y, X, o
endmodule
